# Fritzing sketch analog_station (saved by Fritzing 1.0.5)
circuit board: 15.35cm x 3.5cm
breadboards: 1

parts:
  BME_280 = GY-BMEP280 Barometric Pressure Sensor - Breakout
  MIC = Adafruit MAX4466 Electret Microphone Amplifier [part_number="Adafruit #1063"]
  ESP32-C3 = Esp32-c3 super mini
  MTR1 = Screw terminal - 2 pins [package=THT]
  LED1 = Screw terminal - 2 pins [package=THT]
  MTR2 = Screw terminal - 2 pins [package=THT]
  LED2 = Screw terminal - 2 pins [package=THT]
  MTR3 = Screw terminal - 2 pins [package=THT]
  LED3 = Screw terminal - 2 pins [package=THT]
  SWITCH = Screw terminal - 2 pins [package=THT]

nets:
  N1: BME_280.SCL, ESP32-C3.Pin_7
  N2: BME_280.SDA, ESP32-C3.Pin_8
  N3: BME_280.SDO, MIC.VCC, ESP32-C3.Pin_14
  N4: MIC.OUT, ESP32-C3.Pin_13
  N5: ESP32-C3.Pin_1, LED3.pin2
  N6: ESP32-C3.Pin_2, MTR1.pin2
  N7: ESP32-C3.Pin_3, MTR2.pin2
  N8: ESP32-C3.Pin_6, MTR3.pin2
  N9: ESP32-C3.Pin_9, LED2.pin2
  N10: ESP32-C3.Pin_10, LED1.pin2
  N11: ESP32-C3.Pin_12, SWITCH.pin2

notes:
  THE ANALOG STATION!
  Designed in San Francisco
  for learning and making.

custom parts:
  GY-BMEP280 Barometric Pressure Sensor - Breakout: The BME280 is a chip which was originally designed for the next generation of smartphones. It is made up of a very accurate pressure sensor and an associated temperature sensor which helps calibrate the pressure readings. And just for fun they threw in a pretty solid humidity sensor in there as well! So with an I2C connection you have access to enough weather data to make some pretty good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
  Adafruit MAX4466 Electret Microphone Amplifier: Add an ear to your project with this well-designed electret microphone amplifier. This fully assembled and tested board comes with a 20-20KHz electret microphone soldered on. For the amplification, we use the Maxim MAX4466, an op-amp specifically designed for this delicate task! The amplifier has excellent power supply noise rejection, so this amplifier sounds really good and isn't nearly as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
  Esp32-c3 super mini: ESP32-C3 Development Board ESP32 SuperMini Development Board ESP32 Development Board WiFi Bluetooth.
